# Fritzing sketch Robot2 (saved by Fritzing 0.9.3b)
breadboards: 1

parts:
  Part1 = Arduino Uno (Rev3)
  HC-SR04_|_Ultrasonic_Sensor = HC-SR04 Ultrasonic Distance Sensor
  Back_Right = Basic Servo [part_number=BR]
  Back_Left = Basic Servo [part_number=BL]
  Front_Left = Basic Servo [part_number=FL]
  Front_Right = Basic Servo [part_number=FR]
  Raspberry_Pi_3 = Raspberry Pi 3 [part_number=RPI-3-V1.2]
  Fan = Fan - Ventilador [package=THT]
  R1 = Resistor [tolerance=±5% resistance=2k package="1206 [SMD]"]
  R2 = Resistor [tolerance=±5% resistance=1k package="1206 [SMD]"]

nets (from the breadboard view):
  N1: Part1.D9_PWM, Back_Left.pulse
  N2: Part1.D10_PWM/SS, Front_Left.pulse
  N3: Part1.D5_PWM, Back_Right.pulse
  N4: Part1.D6_PWM, Front_Right.pulse
  VCC: Part1.5V, HC-SR04_|_Ultrasonic_Sensor.VCC, Back_Right.vcc, Back_Left.vcc, Front_Left.vcc, Front_Right.vcc, Fan.5V
  GND: Part1.GND, HC-SR04_|_Ultrasonic_Sensor.GND, Back_Right.gnd, Back_Left.gnd, Front_Left.gnd, Front_Right.gnd, Fan.GND, R1.Pin_1
  N5: HC-SR04_|_Ultrasonic_Sensor.TRIG, Raspberry_Pi_3.GPIO23
  N6: HC-SR04_|_Ultrasonic_Sensor.ECHO, R2.Pin_1
  N7: Raspberry_Pi_3.GPIO24, R1.Pin_0, R2.Pin_0

custom parts:
  Fan - Ventilador: Ventilador de 2 pines, se encuentra comunmente en computadoras de escritorio
